# Fritzing sketch 1_24207933692 (saved by Fritzing 1.0.5)
breadboards: 1

parts:
  Part1 = Arduino Uno (Rev3)
  Part2 = Bluetooth HC-05 Macho

nets:
  N1: Part1.D10_PWM/SS, Part2.TXD
  N2: Part1.D11_PWM/MOSI, Part2.RXD
  5V: Part1.5V, Part2.VCC
  GND: Part1.GND, Part2.GND
